# Fritzing sketch nutscrewer (saved by Fritzing 0.9.2b)
circuit board: 8.46667cm x 5.64444cm
breadboards: 1

parts:
  Bauteil1 = Arduino Nano (Rev3.0)
  DRV_1 = DRV 8825 Stepper Motor Carrier, High Current [part_number="DRV 8825"]
  DRV_2 = DRV 8825 Stepper Motor Carrier, High Current [part_number="DRV 8825"]
  RE1 = Rotary Encoder [package=THT]  # not connected
  M1 = Stepper Motor - Bipolar
  M2 = Stepper Motor - Bipolar
  C1 = Electrolytic Capacitor [capacitance=1µF package="100 mil [THT, electrolytic]"]
  Power_plug1 = Power plug
  S1 = Round Pushbutton
  C2 = Electrolytic Capacitor [capacitance=1µF package="100 mil [THT, electrolytic]"]

nets:
  GND: Bauteil1.GND, DRV_2.GROUND_ST/_MT, C1.-, Power_plug1.GND, S1.leg1
  N1: Bauteil1.D2, S1.leg0
  N2: Bauteil1.D4, DRV_1.ENABLE, DRV_2.ENABLE
  N3: Bauteil1.D5, DRV_1.STEP, DRV_2.STEP
  N4: Bauteil1.D6, DRV_1.DIRECTION, DRV_2.DIRECTION
  VIN: Bauteil1.VIN, DRV_1.VOLTAGE_ST/_MT, DRV_1.GROUND_ST/_MT, DRV_2.VOLTAGE_ST/_MT, C1.+, Power_plug1.VCC, C2.-, C2.+
  N5: Bauteil1.A5, DRV_1.RESET, DRV_1.SLEEP, DRV_2.RESET, DRV_2.SLEEP
  N6: DRV_1.OUT_2B, M1.A
  N7: DRV_1.OUT_2A, M1.C
  N8: DRV_1.OUT_1A, M1.B
  N9: DRV_1.OUT_1B, M1.D
  N10: DRV_2.OUT_2B, M2.A
  N11: DRV_2.OUT_2A, M2.C
  N12: DRV_2.OUT_1A, M2.B
  N13: DRV_2.OUT_1B, M2.D
